# Fritzing sketch DripIrrigationControl-V2 (saved by Fritzing 0.9.3b)
breadboards: 1

parts:
  U1 = NodeMCU V1.0
  SN754410 = H-Bridge [package=THT]
  U2 = TRANSISTOR_NPN_2 [package=to-92]
  R1 = Resistor [tolerance=±5% resistance=220 package="0402 [SMD]"]
  R2 = Resistor [tolerance=±5% resistance=1k package="0402 [SMD]"]
  R3 = Resistor [tolerance=±5% resistance=1k package="0402 [SMD]"]
  R4 = Resistor [tolerance=±5% resistance=10k package="0402 [SMD]"]
  R5 = Resistor [tolerance=±5% resistance=10k package="0402 [SMD]"]
  Solenoid_Valve = Solenoid
  LED = LED - 5mm [color="Red (633nm)" package="5 mm [THT]"]
  J1 = Camdenboss CTB0158-11 [part_number=CTB0158-11 package=THT]
  LCD = LCD1602-I2C
  Flow_Sensor = Camdenboss CTB0158-3 [part_number=FL-408 package=THT]
  S2 = Momentary Switch [package=ksa_sealed_tac_switch]
  J2 = Camdenboss CTB0158-4 [part_number=CTB0158-4 package=THT]

nets:
  N1: U1.D1, J1.pin8
  N2: U1.D2, J1.pin9
  N3: U1.D3, SN754410.1_2EN
  N4: U1.D6, SN754410.2A, R2.Pin_0
  N5: U1.D7, J1.pin3
  GND: U1.GND, SN754410.GND1, SN754410.GND2, U2.E, J1.pin1, J1.pin2
  N6: U1.3V3, R5.Pin_1, J1.pin11
  N7: U1.Vin, SN754410.VCC1, R3.Pin_1, J1.pin6
  N8: SN754410.1A, U2.C, R3.Pin_0
  N9: SN754410.1Y, J1.pin4
  N10: SN754410.2Y, J1.pin5
  N11: U2.B, R2.Pin_1
  N12: R1.Pin_1, J1.pin7
  N13: R4.Pin_1, R5.Pin_0, J1.pin10
  N14: Solenoid_Valve.pin1, J1.terminal_5
  N15: Solenoid_Valve.pin2, J1.terminal_4
  GND_2: LED.cathode, LCD.GND, Flow_Sensor.pin3, J2.terminal_1
  N16: LED.anode, J2.terminal_3
  N17: J1.terminal_2, J2.pin1, J2.pin2
  N18: J1.terminal_3, Flow_Sensor.pin2
  N19: J1.terminal_6, LCD.VCC
  N20: J1.terminal_7, J2.pin3
  N21: J1.terminal_8, LCD.SCL
  N22: J1.terminal_9, LCD.SDA
  N23: J1.terminal_10, J2.pin4
  N24: J1.terminal_11, Flow_Sensor.pin1
  N25: S2.1, J2.terminal_4
  N26: S2.3, J2.terminal_2

custom parts:
  NodeMCU V1.0: ESP8266 based NodeMCU
  LCD1602-I2C: A standard character display, usually with 2x16 characters. Comes in many colors with LCM1602 IIC attached.
